// Logisim project lab6ALU.circ as structural Verilog: 7 circuits, main circuit ALU
// LAB12-ALU
module ALU (
  input  [31:0] ALU_Source_1,
  input  [31:0] ALU_Source_2,
  input  [2:0] ALU_Control,
  output [31:0] ALU_Result
);

  // Probe on ALU_Source_1
  // Probe on ALU_Source_2
  // Probe on ALU_Result

  // Other names for the same wires on the sheet: control[2:0] = ALU_Control; result[31:0] = ALU_Result;
  //   source1[31:0] = ALU_Source_1; source2[31:0] = ALU_Source_2

  // Notes on the sheet:
  //   DO NOT CROSS WIRES
  //   OVER THIS BOX
  //   DO NOT CROSS WIRES
  //   OVER THIS BOX
  //   COMPUTE ALL POSSIBLE OPERATIONS
  //   * YOUR CIRCUIT HERE *
  //   DO NOT CROSS WIRES
  //   OVER THIS BOX
  //   DO NOT CROSS WIRES
  //   OVER THIS BOX
  //   SELECT THE REQUESTED RESULT
  //   * YOUR CIRCUIT HERE *
  //   DO NOT CROSS WIRES
  //   OVER THIS BOX
endmodule

module Ex1 (
  input  [7:0] \input ,
  output Out1,
  output [7:0] Out2
);

  not not_1 (Out2[7], \input [7]);
  and and_1 (Out1, \input [0], \input [7]);

  assign Out2[6:0] = \input [6:0];
endmodule

module Rotr1 (
  input  [15:0] in_1,
  output [15:0] out_2
);


  assign out_2 = {in_1[0], in_1[15:1]};

  // Other names for the same wires on the sheet: _15_high[14:0] = in_1[15:1]; _1_low = in_1[0]
endmodule

module Rotr2 (
  input  [15:0] in_1,
  output [15:0] out_2
);

  wire [15:0] rotr1_1_out_2;

  Rotr1 rotr1_1 (.in_1(in_1), .out_2(rotr1_1_out_2));
  Rotr1 rotr1_2 (.in_1(rotr1_1_out_2), .out_2(out_2));
endmodule

module Rotr4 (
  input  [15:0] in_1,
  output [15:0] out_2
);

  wire [15:0] rotr2_1_out_2;

  Rotr2 rotr2_1 (.in_1(in_1), .out_2(rotr2_1_out_2));
  Rotr2 rotr2_2 (.in_1(rotr2_1_out_2), .out_2(out_2));
endmodule

module Rotr8 (
  input  [15:0] in_1,
  output [15:0] out_2
);

  wire [15:0] rotr4_1_out_2;

  Rotr4 rotr4_1 (.in_1(in_1), .out_2(rotr4_1_out_2));
  Rotr4 rotr4_2 (.in_1(rotr4_1_out_2), .out_2(out_2));
endmodule

module Rotr (
  input  [15:0] A_data,
  input  [3:0] B_num_of_rotr,
  output [15:0] Out
);

  wire [15:0] multiplexer_1_out, multiplexer_2_out, multiplexer_3_out, undriven, undriven_2, undriven_3,
       undriven_4;

  Rotr1 rotr1_1 (.in_1(undriven), .out_2(A_data));
  Multiplexer #(.width(16)) multiplexer_1 (
    .in0(A_data), .in1(undriven), .out(multiplexer_1_out), .sel(B_num_of_rotr[0]));  // open: en
  Rotr2 rotr2_1 (.in_1(undriven_2), .out_2(multiplexer_1_out));
  Multiplexer #(.width(16)) multiplexer_2 (
    .in0(multiplexer_1_out), .in1(undriven_2), .out(multiplexer_2_out), .sel(B_num_of_rotr[1]));  // open: en
  Rotr4 rotr4_1 (.in_1(undriven_3), .out_2(multiplexer_2_out));
  Multiplexer #(.width(16)) multiplexer_3 (
    .in0(multiplexer_2_out), .in1(undriven_3), .out(multiplexer_3_out), .sel(B_num_of_rotr[2]));  // open: en
  Rotr8 rotr8_1 (.in_1(undriven_4), .out_2(multiplexer_3_out));
  Multiplexer #(.width(16)) multiplexer_4 (
    .in0(multiplexer_3_out), .in1(undriven_4), .out(Out), .sel(B_num_of_rotr[3]));  // open: en
endmodule
