// Logisim project alu.circ as structural Verilog: 1 circuit, main circuit main
module main (
  input  [31:0] X,
  input  [31:0] Y,
  input  [5:0] Switch__S,
  input  [2:0] in_4,
  input  [2:0] in_5,
  output Signed_Overflow,
  output [31:0] RESULT,
  output Equal,
  output [2:0] out_9
);

  wire comparator_3_eq, is_add, is_sub, multiplexer_2_out, multiplexer_3_out, not_1_out, not_2_out,
       output_ADD_overflow, output_SUB_overflow, subtractor_1_bout, xor_1_out, xor_2_out, xor_3_out;
  wire [4:0] bit_extender_1_out, bit_extender_2_out, bit_extender_3_out;
  wire [31:0] output_ADD_Unsighed, output_AND, output_be, output_bne, output_OR,
       output_set_less_than_Unsigned, output_sll, output_sra, output_srl, output_SUB_Unsighed;
  wire [31:31] output_ADD_Unsigned;

  assign output_AND = X & Y;  // AND_Gate and_1, 32 bits wide
  assign output_OR = X | Y;  // OR_Gate or_1, 32 bits wide
  Adder #(.width(32)) adder_1 (.a(X), .b(Y), .out(output_ADD_Unsighed));  // open: cin, cout
  Subtractor #(.width(32)) subtractor_1 (
    .a(X), .b(Y), .out(output_SUB_Unsighed), .bout(subtractor_1_bout));  // open: bin
  Comparator #(.width(6)) comparator_1 (.a(Switch__S), .b(6'b100000), .eq(is_add));  // open: gt, lt
  Comparator #(.width(6)) comparator_2 (.a(Switch__S), .b(6'b100010), .eq(is_sub));  // open: gt, lt
  Bit_Extender #(.in_width(32), .out_width(5)) bit_extender_1 (.in(Y), .out(bit_extender_1_out));
  Bit_Extender #(.in_width(32), .out_width(5)) bit_extender_2 (.in(Y), .out(bit_extender_2_out));
  Bit_Extender #(.in_width(32), .out_width(5)) bit_extender_3 (.in(Y), .out(bit_extender_3_out));
  assign output_set_less_than_Unsigned = {{31{1'b0}}, subtractor_1_bout};  // Bit_Extender bit_extender_4
  Shifter #(.width(32)) shifter_1 (.in(X), .\dist (bit_extender_1_out), .out(output_sll));
  Shifter #(.width(32), .shift("lr")) shifter_2 (.in(X), .\dist (bit_extender_2_out), .out(output_srl));
  Shifter #(.width(32), .shift("ar")) shifter_3 (.in(X), .\dist (bit_extender_3_out), .out(output_sra));
  Comparator #(.width(32)) comparator_3 (.a(X), .b(Y), .eq(comparator_3_eq));  // open: gt, lt
  not not_1 (not_1_out, comparator_3_eq);
  assign output_be = {{31{1'b0}}, comparator_3_eq};  // Bit_Extender bit_extender_5
  assign output_bne = {{31{1'b0}}, not_1_out};  // Bit_Extender bit_extender_6
  Multiplexer #(.select(5), .width(32)) multiplexer_1 (
    .in0(output_sll), .in2(output_srl), .in3(output_sra), .in16(output_ADD_Unsighed),
    .in17(output_ADD_Unsighed), .in18(output_SUB_Unsighed), .in19(output_SUB_Unsighed), .in20(output_AND),
    .in21(output_OR), .out(RESULT), .sel({Switch__S[5], Switch__S[3:0]}));  // open: in1, in4, in5, in6, in7, in8, in9, in10, in11, in12, in13, in14, in15, in22, in23, in24, in25, in26, in27, in28, in29, in30, in31, en
  xor xor_1 (xor_1_out, X[31], Y[31]);
  xor xor_2 (xor_2_out, X[31], output_ADD_Unsigned[31]);
  xor xor_3 (xor_3_out, X[31], output_SUB_Unsighed[31]);
  Multiplexer multiplexer_2 (.in0(1'b0), .in1(output_ADD_overflow), .out(multiplexer_2_out), .sel(is_add));  // open: en
  not not_2 (not_2_out, xor_1_out);
  Subtractor #(.width(3)) subtractor_2 (.a(in_4), .b(in_5), .out(out_9));  // open: bin, bout
  Multiplexer multiplexer_3 (.in0(1'b0), .in1(output_SUB_overflow), .out(multiplexer_3_out), .sel(is_sub));  // open: en
  and and_2 (output_ADD_overflow, not_2_out, xor_2_out);
  and and_3 (output_SUB_overflow, xor_1_out, xor_3_out);
  or or_2 (Signed_Overflow, multiplexer_2_out, multiplexer_3_out);
  Comparator #(.width(32)) comparator_4 (.a(X), .b(Y), .eq(Equal));  // open: gt, lt

  // Other names for the same wires on the sheet: input_X[31:0] = X; input_Y[31:0] = Y;
  //   output_load_addr[31:0] = output_ADD_Unsighed; switch[4:0] = {Switch__S[5], Switch__S[3:0]}

  // Notes on the sheet:
  //   INPUTS to your circuit
  //   INPUT to your circuit
  //   add unsigned
  //   sub unsigned
  //   DON'T CHANGE THE INPUTS AND OUTPUTS! IF YOU DO SO, YOU NEED TO MAKE SURE THE PINS ARE IN THE RIGHT PLACES!
  //   X-31
  //   Y-31
  //   OUTPUTS of your circuit
endmodule
