// Logisim project mem.circ as structural Verilog: 1 circuit, main circuit main
module main (
  input  [31:0] Data_Mem_Addr,
  input  [31:0] Data_Mem_In,
  input  ACCESS_BYTE,
  input  MEM_WRITE,
  input  CLOCK,
  output [31:0] Data_Mem_Out
);

  wire not_1_out;
  wire [7:0] multiplexer_1_out;
  wire [31:0] bit_extender_1_out, \return ;

  not not_1 (not_1_out, MEM_WRITE);
  RAM #(.addrWidth(24), .dataWidth(32), .bus("separate")) ram_1 (
    .addr(Data_Mem_Addr[25:2]), .din(Data_Mem_In), .data(\return ), .str(MEM_WRITE), .sel(1'b1), .clk(CLOCK),
    .ld(not_1_out), .clr(1'b0));
  Multiplexer #(.select(2), .width(8)) multiplexer_1 (
    .in0(\return [7:0]), .in1(\return [15:8]), .in2(\return [23:16]), .in3(\return [31:24]),
    .out(multiplexer_1_out), .sel(Data_Mem_Addr[1:0]));  // open: en
  assign bit_extender_1_out = {{24{1'b0}}, multiplexer_1_out};  // Bit_Extender bit_extender_1
  Multiplexer #(.width(32)) multiplexer_2 (
    .in0(\return ), .in1(bit_extender_1_out), .out(Data_Mem_Out), .sel(ACCESS_BYTE));  // open: en

  // Other names for the same wires on the sheet: byte_addr[1:0] = Data_Mem_Addr[1:0]

  // Notes on the sheet:
  //   These are INPUTS to the circuit
  //   These are INPUTS to the circuit
  //   DO NOT CHANGE THE LOCATIONS OF THE INPUTS/OUTPUTS! IF YOU DO SO, YOU NEED TO MAKE SURE THE PINS ARE AT THE RIGHT PLACE!
  //   Yet again, the clock is not an actual clock, but an input, one that will be driven from a higher circuit
  //   This is an OUTPUT to the circuit
endmodule
